# Fritzing sketch WiringDiagram (saved by Fritzing 0.7.10b)
breadboards: 1

parts:
  Teensy++1 = Teensy++ 2.0
  LCD1 = LCD screen
  R1 = Trimmer Potentiometer [maximum_resistance=10kΩ package=THT]
  RE1 = Rotary Encoder [package=THT]
  RE2 = Rotary Encoder [package=THT]
  S1 = Pushbutton [package=THT]
  S2 = Pushbutton [package=THT]

nets:
  N1: Teensy++1.GND#0, Teensy++1.GND#21, LCD1.VSS, LCD1.LED-, R1.leg2, RE1.EncoderPinC, RE2.EncoderPinC, S1.leg0, S2.leg0
  N2: Teensy++1.C4, RE1.EncoderPinA
  N3: Teensy++1.C5, RE1.EncoderPinB
  N4: Teensy++1.C6, RE2.EncoderPinA
  N5: Teensy++1.C7, RE2.EncoderPinB
  N6: Teensy++1.F7, LCD1.DB7
  N7: Teensy++1.F6, LCD1.DB6
  N8: Teensy++1.F5, LCD1.DB5
  N9: Teensy++1.F4, LCD1.DB4
  N10: Teensy++1.F3, LCD1.E
  N11: Teensy++1.F2, LCD1.R/W
  N12: Teensy++1.F1, LCD1.RS
  N13: Teensy++1.F0, S2.leg1
  N14: Teensy++1.E6, S1.leg1
  VCC: Teensy++1.VCC, LCD1.VDD, LCD1.LED+, R1.leg1
  N15: LCD1.V0, R1.wiper
